# Fritzing sketch rfid-buzzer-led (saved by Fritzing 0.9.3b)

parts:
  Componente1 = RFID-RC522-v3
  U1 = NodeMCU V3.0
  J1 = Piezo Speaker

nets:
  N1: Componente1.SDA, U1.D5
  N2: Componente1.SCK, U1.D3
  N3: Componente1.MOSI, U1.D4
  N4: Componente1.MISO, U1.D2
  GND: Componente1.GND, U1.GND, J1.pin1
  N5: Componente1.RST, U1.D1
  3.3V: Componente1.3.3V, U1.3V3
  N6: U1.D6, J1.pin2

custom parts:
  RFID-RC522-v3: A simple China made RFID-RC522 Reader (6x4 cm); do check the pin labels, as this is a MFRC522 based clone.
  NodeMCU V3.0: ESP8266 based NodeMCU
